// Logisim project 1_2.circ as structural Verilog: 1 circuit, main circuit main
module main (
  input  A,
  input  B,
  input  C,
  output SUM,
  output out_5
);

  wire and_1_out, and_2_out, xor_1_out;

  xor xor_1 (xor_1_out, A, B);
  and and_1 (and_1_out, B, A);
  xor xor_2 (SUM, xor_1_out, C);
  and and_2 (and_2_out, xor_1_out, C);
  or or_1 (out_5, and_2_out, and_1_out);

  // Notes on the sheet:
  //   CARRY
endmodule
