// Logisim project B110_2bitFull Adder.circ as structural Verilog: 1 circuit, main circuit main
module main (
  input  A1,
  input  B1,
  input  A0,
  input  B0,
  input  Cin,
  output S1,
  output S2,
  output S0
);

  wire and_1_out, and_2_out, and_3_out, and_4_out, or_2_out, xor_1_out, xor_2_out;

  xor xor_1 (xor_1_out, A1, B1);
  and and_1 (and_1_out, A1, B1);
  xor xor_2 (xor_2_out, A0, B0);
  and and_2 (and_2_out, A0, B0);
  xor xor_3 (S1, xor_1_out, or_2_out);
  and and_3 (and_3_out, xor_1_out, or_2_out);
  xor xor_4 (S0, xor_2_out, Cin);
  and and_4 (and_4_out, xor_2_out, Cin);
  or or_1 (S2, and_3_out, and_1_out);
  or or_2 (or_2_out, and_4_out, and_2_out);

  // Notes on the sheet:
  //   Input = A1 A0 + B1 B0
  //   Output = S2 S1 S0
endmodule
