// Logisim project B110_2bitFull Subtractor.circ as structural Verilog: 1 circuit, main circuit main
module main (
  input  Bin,
  input  A0,
  input  B0,
  input  A1,
  input  B1,
  output D1,
  output D2,
  output Bout2
);

  wire and_1_out, and_2_out, and_3_out, and_4_out, not_1_out, not_2_out, not_3_out, not_4_out, or_1_out,
       xor_1_out, xor_2_out;

  not not_1 (not_1_out, A0);
  not not_2 (not_2_out, A1);
  xor xor_1 (xor_1_out, A0, B0);
  and and_1 (and_1_out, B0, not_1_out);
  xor xor_2 (xor_2_out, A1, B1);
  and and_2 (and_2_out, B1, not_2_out);
  not not_3 (not_3_out, xor_1_out);
  not not_4 (not_4_out, xor_2_out);
  xor xor_3 (D1, Bin, xor_1_out);
  and and_3 (and_3_out, not_3_out, Bin);
  xor xor_4 (D2, or_1_out, xor_2_out);
  and and_4 (and_4_out, not_4_out, or_1_out);
  or or_1 (or_1_out, and_3_out, and_1_out);
  or or_2 (Bout2, and_4_out, and_2_out);

  // Notes on the sheet:
  //   Input A1 A0 - B1 B0
  //   Output - D2 D1
endmodule
