// Logisim project B110_4bitFull Subtractor.circ as structural Verilog: 1 circuit, main circuit main
module main (
  input  Bin,
  input  A0,
  input  B0,
  input  A1,
  input  B1,
  input  A2,
  input  B2,
  input  A3,
  input  B3,
  output D0,
  output D1,
  output D2,
  output D3,
  output Bout4
);

  wire and_1_out, and_2_out, and_3_out, and_4_out, and_5_out, and_6_out, and_7_out, and_8_out, not_1_out,
       not_2_out, not_3_out, not_4_out, not_5_out, not_6_out, not_7_out, not_8_out, or_1_out, or_2_out,
       or_3_out, xor_1_out, xor_2_out, xor_3_out, xor_4_out;

  not not_1 (not_1_out, A0);
  not not_2 (not_2_out, A1);
  not not_3 (not_3_out, A2);
  not not_4 (not_4_out, A3);
  xor xor_1 (xor_1_out, A0, B0);
  and and_1 (and_1_out, B0, not_1_out);
  xor xor_2 (xor_2_out, A1, B1);
  and and_2 (and_2_out, B1, not_2_out);
  xor xor_3 (xor_3_out, A2, B2);
  and and_3 (and_3_out, B2, not_3_out);
  xor xor_4 (xor_4_out, A3, B3);
  and and_4 (and_4_out, B3, not_4_out);
  not not_5 (not_5_out, xor_1_out);
  not not_6 (not_6_out, xor_2_out);
  not not_7 (not_7_out, xor_3_out);
  not not_8 (not_8_out, xor_4_out);
  xor xor_5 (D0, Bin, xor_1_out);
  and and_5 (and_5_out, not_5_out, Bin);
  xor xor_6 (D1, or_1_out, xor_2_out);
  and and_6 (and_6_out, not_6_out, or_1_out);
  xor xor_7 (D2, or_2_out, xor_3_out);
  and and_7 (and_7_out, not_7_out, or_2_out);
  xor xor_8 (D3, or_3_out, xor_4_out);
  and and_8 (and_8_out, not_8_out, or_3_out);
  or or_1 (or_1_out, and_5_out, and_1_out);
  or or_2 (or_2_out, and_6_out, and_2_out);
  or or_3 (or_3_out, and_7_out, and_3_out);
  or or_4 (Bout4, and_8_out, and_4_out);

  // Notes on the sheet:
  //   Input = A3 A2 A1 A0 - B3 B2 B1 B0
  //   Output = D3 D2 D1 D0
  //   Bout1
  //   Bout2
  //   Bout3
endmodule
