// Logisim project B110_4bitFullAdder.circ as structural Verilog: 2 circuits, main circuit main
module main (
  input  Ao,
  input  Bo,
  input  A2,
  input  A3,
  input  A1,
  input  B2,
  input  B3,
  input  Cin,
  input  B1,
  output So,
  output S1,
  output S2,
  output S3,
  output S4
);

  wire full_adder_1_out_5, full_adder_2_out_5, full_adder_3_out_5;

  Full_Adder full_adder_1 (.Ao(Ao), .Bo(Bo), .Cin(Cin), .out_4(So), .out_5(full_adder_1_out_5));
  Full_Adder full_adder_2 (.Ao(full_adder_1_out_5), .Bo(A1), .Cin(B1), .out_4(S1), .out_5(full_adder_2_out_5));
  Full_Adder full_adder_3 (.Ao(full_adder_2_out_5), .Bo(A2), .Cin(B2), .out_4(S2), .out_5(full_adder_3_out_5));
  Full_Adder full_adder_4 (.Ao(full_adder_3_out_5), .Bo(A3), .Cin(B3), .out_4(S3), .out_5(S4));

  // Notes on the sheet:
  //   Input - A3 A2 A1 A0 + B3 B2 B1 B0
  //   Output - S4 S3 S2 S1 S0
  //   Full Adder
  //   Full Adder
  //   Full Adder
  //   Full Adder
endmodule

module Full_Adder (
  input  Ao,
  input  Bo,
  input  Cin,
  output out_4,
  output out_5
);

  wire and_1_out, and_2_out, xor_1_out;

  xor xor_1 (xor_1_out, Bo, Cin);
  and and_1 (and_1_out, Bo, Cin);
  xor xor_2 (out_4, Ao, xor_1_out);
  and and_2 (and_2_out, xor_1_out, Ao);
  xor xor_3 (out_5, and_2_out, and_1_out);
endmodule
