// Logisim project B110_8bitFull Subtractor.circ as structural Verilog: 1 circuit, main circuit main
module main (
  input  Bin,
  input  A0,
  input  B0,
  input  A1,
  input  B1,
  input  A2,
  input  B2,
  input  A3,
  input  B3,
  input  A4,
  input  B4,
  input  A5,
  input  B5,
  input  A6,
  input  B6,
  input  A7,
  input  B7,
  output D0,
  output D1,
  output D2,
  output D3,
  output D4,
  output D5,
  output D6,
  output D7,
  output Bout8
);

  wire and_1_out, and_2_out, and_3_out, and_4_out, and_5_out, and_6_out, and_7_out, and_8_out, and_9_out,
       and_10_out, and_11_out, and_12_out, and_13_out, and_14_out, and_15_out, and_16_out, not_1_out,
       not_2_out, not_3_out, not_4_out, not_5_out, not_6_out, not_7_out, not_8_out, not_9_out, not_10_out,
       not_11_out, not_12_out, not_13_out, not_14_out, not_15_out, not_16_out, or_1_out, or_2_out, or_3_out,
       or_4_out, or_5_out, or_6_out, or_7_out, xor_1_out, xor_2_out, xor_3_out, xor_4_out, xor_5_out,
       xor_6_out, xor_7_out, xor_8_out;

  not not_1 (not_1_out, A0);
  not not_2 (not_2_out, A1);
  not not_3 (not_3_out, A2);
  not not_4 (not_4_out, A3);
  not not_5 (not_5_out, A4);
  not not_6 (not_6_out, A5);
  not not_7 (not_7_out, A6);
  not not_8 (not_8_out, A7);
  xor xor_1 (xor_1_out, A0, B0);
  and and_1 (and_1_out, B0, not_1_out);
  xor xor_2 (xor_2_out, A1, B1);
  and and_2 (and_2_out, B1, not_2_out);
  xor xor_3 (xor_3_out, A2, B2);
  and and_3 (and_3_out, B2, not_3_out);
  xor xor_4 (xor_4_out, A3, B3);
  and and_4 (and_4_out, B3, not_4_out);
  xor xor_5 (xor_5_out, A4, B4);
  and and_5 (and_5_out, B4, not_5_out);
  xor xor_6 (xor_6_out, A5, B5);
  and and_6 (and_6_out, B5, not_6_out);
  xor xor_7 (xor_7_out, A6, B6);
  and and_7 (and_7_out, B6, not_7_out);
  xor xor_8 (xor_8_out, A7, B7);
  and and_8 (and_8_out, B7, not_8_out);
  not not_9 (not_9_out, xor_1_out);
  not not_10 (not_10_out, xor_2_out);
  not not_11 (not_11_out, xor_3_out);
  not not_12 (not_12_out, xor_4_out);
  not not_13 (not_13_out, xor_5_out);
  not not_14 (not_14_out, xor_6_out);
  not not_15 (not_15_out, xor_7_out);
  not not_16 (not_16_out, xor_8_out);
  xor xor_9 (D0, Bin, xor_1_out);
  and and_9 (and_9_out, not_9_out, Bin);
  xor xor_10 (D1, or_1_out, xor_2_out);
  and and_10 (and_10_out, not_10_out, or_1_out);
  xor xor_11 (D2, or_2_out, xor_3_out);
  and and_11 (and_11_out, not_11_out, or_2_out);
  xor xor_12 (D3, or_3_out, xor_4_out);
  and and_12 (and_12_out, not_12_out, or_3_out);
  xor xor_13 (D4, or_4_out, xor_5_out);
  and and_13 (and_13_out, not_13_out, or_4_out);
  xor xor_14 (D5, or_5_out, xor_6_out);
  and and_14 (and_14_out, not_14_out, or_5_out);
  xor xor_15 (D6, or_6_out, xor_7_out);
  and and_15 (and_15_out, not_15_out, or_6_out);
  xor xor_16 (D7, or_7_out, xor_8_out);
  and and_16 (and_16_out, not_16_out, or_7_out);
  or or_1 (or_1_out, and_9_out, and_1_out);
  or or_2 (or_2_out, and_10_out, and_2_out);
  or or_3 (or_3_out, and_11_out, and_3_out);
  or or_4 (or_4_out, and_12_out, and_4_out);
  or or_5 (or_5_out, and_13_out, and_5_out);
  or or_6 (or_6_out, and_14_out, and_6_out);
  or or_7 (or_7_out, and_15_out, and_7_out);
  or or_8 (Bout8, and_16_out, and_8_out);

  // Notes on the sheet:
  //   Input = A7 A6 A5 A4 A3 A2 A1 A0 - B7 B6 B5 B4 B3 B2 B1 B0
  //   Output = D7 D6 D5 D4 D3 D2 D1 D0
  //   Bout1
  //   Bout2
  //   Bout3
  //   Bout5
  //   Bout6
  //   Bout7
  //   Bout4
endmodule
