// Logisim project B110_8bitFullAdder.circ as structural Verilog: 2 circuits, main circuit main
module main (
  input  Ao,
  input  Bo,
  input  A2,
  input  A3,
  input  A4,
  input  A5,
  input  A6,
  input  A7,
  input  A1,
  input  in_10,
  input  B2,
  input  B3,
  input  B4,
  input  B5,
  input  B6,
  input  B7,
  input  B1,
  output So,
  output S1,
  output S2,
  output S3,
  output S4,
  output S5,
  output S6,
  output S7,
  output S8
);

  wire full_adder_1_out_5, full_adder_2_out_5, full_adder_3_out_5, full_adder_4_out_5, full_adder_5_out_5,
       full_adder_6_out_5, full_adder_7_out_5;

  Full_Adder full_adder_1 (.in_1(Ao), .in_2(Bo), .in_3(in_10), .out_4(So), .out_5(full_adder_1_out_5));
  Full_Adder full_adder_2 (.in_1(full_adder_1_out_5), .in_2(A1), .in_3(B1), .out_4(S1), .out_5(full_adder_2_out_5));
  Full_Adder full_adder_3 (.in_1(full_adder_2_out_5), .in_2(A2), .in_3(B2), .out_4(S2), .out_5(full_adder_3_out_5));
  Full_Adder full_adder_4 (.in_1(full_adder_3_out_5), .in_2(A3), .in_3(B3), .out_4(S3), .out_5(full_adder_4_out_5));
  Full_Adder full_adder_5 (.in_1(full_adder_4_out_5), .in_2(A4), .in_3(B4), .out_4(S4), .out_5(full_adder_5_out_5));
  Full_Adder full_adder_6 (.in_1(full_adder_5_out_5), .in_2(A5), .in_3(B5), .out_4(S5), .out_5(full_adder_6_out_5));
  Full_Adder full_adder_7 (.in_1(full_adder_6_out_5), .in_2(A6), .in_3(B6), .out_4(S6), .out_5(full_adder_7_out_5));
  Full_Adder full_adder_8 (.in_1(full_adder_7_out_5), .in_2(A7), .in_3(B7), .out_4(S7), .out_5(S8));

  // Notes on the sheet:
  //   Cin
  //   Input = A7 A6 A5 A4 A3 A2 A1 A0 + B7 B6 B5 B4 B3 B2 B1 B0
  //   OUTPUT = S8 S7 S6 S5 S4 S3 S2 S1 S0
  //   Full Adder
  //   Full Adder
  //   Full Adder
  //   Full Adder
  //   Full adder
  //   Full adder
  //   Full adder
  //   Full adder
endmodule

module Full_Adder (
  input  in_1,
  input  in_2,
  input  in_3,
  output out_4,
  output out_5
);

  wire and_1_out, and_2_out, xor_1_out;

  xor xor_1 (xor_1_out, in_2, in_3);
  and and_1 (and_1_out, in_2, in_3);
  xor xor_2 (out_4, in_1, xor_1_out);
  and and_2 (and_2_out, xor_1_out, in_1);
  xor xor_3 (out_5, and_2_out, and_1_out);
endmodule
