// Logisim project B110_fullSubstractor.circ as structural Verilog: 1 circuit, main circuit main
module main (
  input  A,
  input  B,
  input  Borrow___in,
  output Diff,
  output Borrow___out
);

  wire and_1_out, and_2_out, not_1_out, not_2_out, xor_1_out;

  not not_1 (not_1_out, A);
  xor xor_1 (xor_1_out, A, B);
  and and_1 (and_1_out, not_1_out, B);
  not not_2 (not_2_out, xor_1_out);
  xor xor_2 (Diff, xor_1_out, Borrow___in);
  and and_2 (and_2_out, not_2_out, Borrow___in);
  or or_1 (Borrow___out, and_2_out, and_1_out);
endmodule
