// Logisim project B110_halfAdder.circ as structural Verilog: 1 circuit, main circuit main
module main (
  input  A,
  input  B,
  output Sum,
  output Carry
);

  xor xor_1 (Sum, A, B);
  and and_1 (Carry, A, B);

  // Notes on the sheet:
  //   Input - 1
  //   Input -2
endmodule
