// Logisim project B110_halfSubtractor.circ as structural Verilog: 1 circuit, main circuit main
module main (
  input  Input_1,
  input  Input_2,
  output Difference,
  output Borrow
);

  wire not_1_out;

  xor xor_1 (Difference, Input_1, Input_2);
  not not_1 (not_1_out, Input_1);
  and and_1 (Borrow, not_1_out, Input_2);

  // Notes on the sheet:
  //   B
  //   A
endmodule
