// Logisim project 1.circ as structural Verilog: 1 circuit, main circuit main
module main (
  input  A,
  input  B,
  output sum,
  output carry
);

  and and_1 (carry, B, A);
  xor xor_1 (sum, A, B);
endmodule
