// Logisim project 4bit 1.2.circ as structural Verilog: 1 circuit, main circuit main
module main (
  input  in_1,
  input  in_2,
  input  in_3,
  input  in_4,
  input  in_5,
  input  in_6,
  input  in_7,
  input  in_8,
  output out_9,
  output out_10,
  output out_11,
  output out_12,
  output out_13
);

  wire and_1_out, and_2_out, and_3_out, and_4_out, and_5_out, and_6_out, and_7_out, or_1_out, xor_2_out;

  xor xor_1 (out_9, in_2, in_7);
  and and_1 (and_1_out, in_7, in_2);
  xor xor_2 (xor_2_out, in_1, in_1);
  xor xor_3 (out_10, xor_2_out, and_1_out);
  and and_2 (and_2_out, and_1_out, and_1_out);
  and and_3 (and_3_out, in_1, in_1);
  or or_1 (or_1_out, and_2_out, and_3_out);
  xor xor_4 (or_1_out, in_3, in_6);
  xor xor_5 (out_11, or_1_out, or_1_out);
  and and_4 (and_4_out, or_1_out, or_1_out);
  and and_5 (and_5_out, in_6, in_3);
  or or_2 (in_4, and_4_out, and_5_out);
  xor xor_6 (in_4, in_4, in_4);
  xor xor_7 (out_12, in_4, in_4);
  and and_6 (and_6_out, in_4, in_4);
  and and_7 (and_7_out, in_4, in_4);
  or or_3 (out_13, and_6_out, and_7_out);

  assign in_5 = in_1;
  assign in_8 = in_4;
endmodule
