// Logisim project 8bit 1.1.circ as structural Verilog: 1 circuit, main circuit main
module main (
  input  in_1,
  input  in_2,
  input  in_3,
  input  in_4,
  input  in_5,
  input  in_6,
  input  in_7,
  input  in_8,
  input  in_9,
  input  in_10,
  input  in_11,
  input  in_12,
  input  in_13,
  input  in_14,
  input  in_15,
  input  in_16,
  input  in_17,
  input  in_18,
  input  in_19,
  input  in_20,
  input  in_21,
  input  in_22,
  input  in_23,
  input  in_24,
  input  in_25,
  output out_26
);

  wire and_1_out, and_2_out, and_3_out, and_4_out, and_5_out, and_6_out, and_7_out, and_8_out, and_9_out,
       and_10_out, and_11_out, and_12_out, and_13_out, and_14_out, and_15_out, and_16_out, xor_3_out,
       xor_4_out, xor_7_out, xor_8_out, xor_11_out, xor_12_out, xor_15_out, xor_16_out;

  xor xor_1 (in_1, in_1, in_1);
  xor xor_2 (in_17, in_17, in_17);
  and and_1 (and_1_out, in_17, in_17);
  and and_2 (and_2_out, in_17, in_17);
  xor xor_3 (xor_3_out, in_1, in_1);
  and and_3 (and_3_out, in_1, in_1);
  and and_4 (and_4_out, in_1, in_1);
  xor xor_4 (xor_4_out, in_17, in_17);
  or or_1 (in_2, and_3_out, and_4_out);
  or or_2 (in_16, and_1_out, and_2_out);
  xor xor_5 (in_2, in_2, in_2);
  xor xor_6 (in_16, in_16, in_16);
  and and_5 (and_5_out, in_2, in_2);
  and and_6 (and_6_out, in_2, in_2);
  xor xor_7 (xor_7_out, in_2, in_2);
  xor xor_8 (xor_8_out, in_16, in_16);
  and and_7 (and_7_out, in_16, in_16);
  and and_8 (and_8_out, in_16, in_16);
  or or_3 (in_3, and_5_out, and_6_out);
  or or_4 (in_14, and_7_out, and_8_out);
  xor xor_9 (in_3, in_3, in_3);
  xor xor_10 (in_14, in_14, in_14);
  xor xor_11 (xor_11_out, in_3, in_3);
  and and_9 (and_9_out, in_3, in_3);
  and and_10 (and_10_out, in_3, in_3);
  xor xor_12 (xor_12_out, in_14, in_14);
  and and_11 (and_11_out, in_14, in_14);
  and and_12 (and_12_out, in_14, in_14);
  or or_5 (in_4, and_9_out, and_10_out);
  or or_6 (in_15, and_11_out, and_12_out);
  xor xor_13 (in_4, in_4, in_4);
  xor xor_14 (in_15, in_15, in_15);
  xor xor_15 (xor_15_out, in_4, in_4);
  and and_13 (and_13_out, in_4, in_4);
  and and_14 (and_14_out, in_4, in_4);
  and and_15 (and_15_out, in_15, in_15);
  and and_16 (and_16_out, in_15, in_15);
  or or_7 (in_17, and_13_out, and_14_out);
  xor xor_16 (xor_16_out, in_15, in_15);
  or or_8 (out_26, and_15_out, and_16_out);

  assign in_5 = in_1;
  assign in_7 = in_2;
  assign in_9 = in_3;
  assign in_11 = in_4;
  assign in_13 = in_1;
  assign in_18 = in_14;
  assign in_20 = in_15;
  assign in_22 = in_16;
  assign in_24 = in_17;
endmodule
