// Logisim project half_sub.circ as structural Verilog: 1 circuit, main circuit main
module main (
  input  A,
  input  B,
  output D___A_B,
  output Bo
);

  wire not_1_out;

  not not_1 (not_1_out, A);
  xor xor_1 (D___A_B, A, B);
  and and_1 (Bo, not_1_out, B);
endmodule
