// Logisim project U20CS110_Assignment-5_CO.circ as structural Verilog: 3 circuits, main circuit main
module main (
  input  b2,
  input  b0,
  input  b1,
  input  a0,
  input  a1,
  input  a2,
  input  a3,
  output s0,
  output s1,
  output s2,
  output s3,
  output s4,
  output s5,
  output s6
);

  wire and_2_out, and_3_out, and_4_out, and_5_out, and_6_out, and_7_out, and_8_out, and_9_out, and_10_out,
       and_11_out, and_12_out, full_adder_1_carry, full_adder_1_sum, full_adder_2_carry, full_adder_2_sum,
       full_adder_3_carry, full_adder_4_carry, half_adder_1_carry, half_adder_2_carry, half_adder_2_sum,
       half_adder_3_carry;

  and and_1 (s0, b0, a0);
  and and_2 (and_2_out, b0, a1);
  and and_3 (and_3_out, b0, a2);
  and and_4 (and_4_out, b0, a3);
  and and_5 (and_5_out, b1, a0);
  and and_6 (and_6_out, b1, a1);
  and and_7 (and_7_out, b1, a2);
  and and_8 (and_8_out, b1, a3);
  half_adder half_adder_1 (.a(and_5_out), .b(and_2_out), .sum(s1), .carry(half_adder_1_carry));
  full_adder full_adder_1 (
    .a(half_adder_1_carry), .b(and_6_out), .Cin(and_3_out), .sum(full_adder_1_sum), .carry(full_adder_1_carry));
  full_adder full_adder_2 (
    .a(full_adder_1_carry), .b(and_7_out), .Cin(and_4_out), .sum(full_adder_2_sum), .carry(full_adder_2_carry));
  half_adder half_adder_2 (.a(full_adder_2_carry), .b(and_8_out), .sum(half_adder_2_sum), .carry(half_adder_2_carry));
  and and_9 (and_9_out, b2, a0);
  and and_10 (and_10_out, b2, a1);
  and and_11 (and_11_out, b2, a2);
  and and_12 (and_12_out, b2, a3);
  half_adder half_adder_3 (.a(and_9_out), .b(full_adder_1_sum), .sum(s2), .carry(half_adder_3_carry));
  full_adder full_adder_3 (
    .a(half_adder_3_carry), .b(and_10_out), .Cin(full_adder_2_sum), .sum(s3), .carry(full_adder_3_carry));
  full_adder full_adder_4 (
    .a(full_adder_3_carry), .b(and_11_out), .Cin(half_adder_2_sum), .sum(s4), .carry(full_adder_4_carry));
  full_adder full_adder_5 (.a(full_adder_4_carry), .b(and_12_out), .Cin(half_adder_2_carry), .sum(s5), .carry(s6));

  // Notes on the sheet:
  //   a0
  //   a1
  //   a2
  //   a3
  //   HF
  //   FA
  //   FA
  //   HA
  //   a0
  //   a1
  //   a2
  //   a3
  //   HA
  //   FA
  //   FA
  //   FA
endmodule

module full_adder (
  input  a,
  input  b,
  input  Cin,
  output sum,
  output carry
);

  wire and_1_out, and_2_out, xor_1_out;

  xor xor_1 (xor_1_out, a, b);
  and and_1 (and_1_out, b, a);
  xor xor_2 (sum, xor_1_out, Cin);
  and and_2 (and_2_out, xor_1_out, Cin);
  or or_1 (carry, and_2_out, and_1_out);
endmodule

module half_adder (
  input  a,
  input  b,
  output sum,
  output carry
);

  xor xor_1 (sum, a, b);
  and and_1 (carry, a, b);
endmodule
