// Logisim project 1and2 (2).circ as structural Verilog: 1 circuit, main circuit main
module main (
  input  [7:0] in_1,
  input  [7:0] in_2,
  input  [7:0] in_3,
  input  in_4,
  input  in_5,
  input  in_6,
  input  in_7,
  input  in_8,
  output [7:0] out_9,
  output [7:0] out_10
);

  wire clock_1_out;

  Clock clock_1 (.out(clock_1_out));
  RAM #(.bus("separate")) ram_1 (
    .addr(in_1), .din(in_3), .data(out_9), .str(in_4), .sel(in_6), .clk(clock_1_out), .ld(in_7), .clr(in_8));
  _7_Segment_Display u_7_segment_display_1 (
    .g(out_9[3]), .f(out_9[2]), .a(out_9[1]), .b(out_9[0]), .e(out_9[4]), .d(out_9[5]), .c(out_9[6]),
    .dp(out_9[7]));
  ROM rom_1 (.addr(in_2), .data(out_10), .sel(in_5));

  // Notes on the sheet:
  //   contents of rom_1 (hex, n*v repeats v):
  //   aa 0 2 0 0 ff 0 ff 0 dd
endmodule
