// Logisim project 1.circ as structural Verilog: 1 circuit, main circuit main
module main (
  input  [7:0] address,
  input  [7:0] address_2,
  input  [7:0] data,
  input  [7:0] data_2,
  input  sel,
  input  load,
  input  select,
  input  load_2,
  input  str,
  input  clr,
  input  store,
  input  enable,
  input  clear,
  input  clear_2,
  input  [7:0] ADDRESS_3,
  input  in_16,
  output [7:0] \output ,
  output [7:0] output_2,
  output [7:0] out_19,
  output [7:0] Output_3
);

  wire clock_1_out, clock_2_out, clock_3_out;

  Clock clock_1 (.out(clock_1_out));
  RAM #(.bus("separate")) ram_1 (
    .addr(address), .din(data), .data(\output ), .str(str), .sel(sel), .clk(clock_1_out), .ld(load), .clr(clr));
  ROM rom_1 (.addr(ADDRESS_3), .data(Output_3), .sel(in_16));
  Clock clock_2 (.out(clock_2_out));
  RAM #(.bus("separate")) ram_2 (
    .addr(address_2), .din(data_2), .data(output_2), .str(store), .sel(select), .clk(clock_2_out),
    .ld(load_2), .clr(clear_2));
  Clock clock_3 (.out(clock_3_out));
  Register register (.D(output_2), .en(enable), .Q(out_19), .clk(clock_3_out), .clr(clear));

  // Notes on the sheet:
  //   RAM
  //   clock
  //   ROM
  //   contents of rom_1 (hex, n*v repeats v):
  //   1 8 12 14 69*0 2
  //   RAM
  //   clock
  //   clock
endmodule
