// Logisim project 2 - Copy.circ as structural Verilog: 1 circuit, main circuit Binary to Decimal
module Binary_to_Decimal (
  input  h,
  input  g,
  input  f,
  input  e,
  input  d,
  input  c,
  input  b2,
  input  a2,
  output a,
  output b,
  output c2,
  output d2,
  output e2,
  output f2,
  output g2
);

  wire and_1_out, and_2_out, and_3_out, and_4_out, and_5_out, and_6_out, and_7_out, and_8_out, and_9_out,
       and_10_out, and_11_out, and_12_out, and_13_out, and_14_out, and_15_out, and_16_out, not_1_out,
       not_2_out, not_3_out, not_4_out, not_5_out, not_6_out, not_7_out, not_8_out, not_9_out, not_10_out,
       not_11_out, not_12_out, not_13_out, not_14_out, not_15_out, not_16_out, not_17_out, not_18_out,
       not_19_out, not_20_out, not_21_out;

  not not_1 (not_1_out, c);
  and and_1 (and_1_out, not_1_out, not_2_out);
  not not_2 (not_2_out, a2);
  and and_2 (and_2_out, c, a2);
  not not_3 (not_3_out, c);
  not not_4 (not_4_out, b2);
  and and_3 (and_3_out, not_4_out, not_5_out);
  not not_5 (not_5_out, a2);
  and and_4 (and_4_out, b2, a2);
  not not_6 (not_6_out, b2);
  or or_1 (c2, not_6_out, a2, c);
  not not_7 (not_7_out, c);
  and and_5 (and_5_out, not_7_out, not_8_out);
  not not_8 (not_8_out, a2);
  not not_9 (not_9_out, c);
  and and_6 (and_6_out, not_9_out, b2);
  and and_7 (and_7_out, b2, not_10_out);
  not not_10 (not_10_out, a2);
  and and_8 (and_8_out, c, not_11_out, a2);
  not not_11 (not_11_out, b2);
  not not_12 (not_12_out, c);
  and and_9 (and_9_out, not_12_out, not_13_out);
  not not_13 (not_13_out, a2);
  and and_10 (and_10_out, b2, not_14_out);
  not not_14 (not_14_out, a2);
  not not_15 (not_15_out, b2);
  and and_11 (and_11_out, not_15_out, not_16_out);
  not not_16 (not_16_out, a2);
  and and_12 (and_12_out, c, not_17_out);
  not not_17 (not_17_out, b2);
  and and_13 (and_13_out, c, not_18_out);
  not not_18 (not_18_out, a2);
  not not_19 (not_19_out, c);
  and and_14 (and_14_out, not_19_out, b2);
  and and_15 (and_15_out, c, not_20_out);
  not not_20 (not_20_out, b2);
  and and_16 (and_16_out, c, not_21_out);
  not not_21 (not_21_out, a2);
  or or_2 (a, and_1_out, b2, and_2_out, d);
  or or_3 (b, not_3_out, and_3_out, and_4_out);
  or or_4 (d2, and_5_out, and_6_out, and_7_out, and_8_out, d);
  or or_5 (e2, and_9_out, and_10_out);
  or or_6 (f2, and_11_out, and_12_out, and_13_out, d);
  or or_7 (g2, and_14_out, and_15_out, and_16_out, d);
endmodule
