// Logisim project 7_segment.circ as structural Verilog: 3 circuits, main circuit main
module main (
  input  in_1,
  input  in_2,
  input  in_3,
  input  in_4,
  input  in_5,
  input  in_6,
  input  in_7,
  input  in_8,
  input  in_9,
  input  in_10,
  input  in_11,
  input  in_12,
  input  in_13,
  input  in_14,
  input  in_15,
  input  in_16,
  input  in_17,
  input  in_18,
  input  in_19,
  input  in_20,
  input  in_21,
  input  in_22,
  input  in_23,
  input  in_24,
  input  in_25,
  input  in_26,
  input  in_27,
  input  in_28,
  input  in_29,
  input  in_30,
  input  in_31,
  input  in_32,
  input  in_33,
  input  in_34
);

  wire n7segalpha_1_a_2, n7segalpha_1_b_2, n7segalpha_1_c, n7segalpha_1_d, n7segalpha_1_e, n7segalpha_1_f,
       n7segalpha_1_g, n7segalpha_2_a_2, n7segalpha_2_b_2, n7segalpha_2_c, n7segalpha_2_d, n7segalpha_2_e,
       n7segalpha_2_f, n7segalpha_2_g, n7segalpha_3_a_2, n7segalpha_3_b_2, n7segalpha_3_c, n7segalpha_3_d,
       n7segalpha_3_e, n7segalpha_3_f, n7segalpha_3_g, n7segment_1_a_2, n7segment_1_b_2, n7segment_1_c_2,
       n7segment_1_d_2, n7segment_1_e, n7segment_1_f, n7segment_1_g, n7segment_2_a_2, n7segment_2_b_2,
       n7segment_2_c_2, n7segment_2_d_2, n7segment_2_e, n7segment_2_f, n7segment_2_g, n7segment_3_a_2,
       n7segment_3_b_2, n7segment_3_c_2, n7segment_3_d_2, n7segment_3_e, n7segment_3_f, n7segment_3_g,
       n7segment_4_a_2, n7segment_4_b_2, n7segment_4_c_2, n7segment_4_d_2, n7segment_4_e, n7segment_4_f,
       n7segment_4_g, n7segment_5_a_2, n7segment_5_b_2, n7segment_5_c_2, n7segment_5_d_2, n7segment_5_e,
       n7segment_5_f, n7segment_5_g;

  _7_Segment_Display u_7_segment_display_1 (
    .g(n7segalpha_1_g), .f(n7segalpha_1_a_2), .a(n7segalpha_1_f), .b(n7segalpha_1_e), .e(n7segalpha_1_b_2),
    .d(n7segalpha_1_c), .c(n7segalpha_1_d), .dp(in_7));
  _7segAlpha u_7segalpha_1 (
    .A(in_11), .B(in_3), .a_2(n7segalpha_1_a_2), .b_2(n7segalpha_1_b_2), .c(n7segalpha_1_c),
    .d(n7segalpha_1_d), .e(n7segalpha_1_e), .f(n7segalpha_1_f), .g(n7segalpha_1_g));
  _7_Segment_Display u_7_segment_display_2 (
    .g(n7segalpha_2_g), .f(n7segalpha_2_a_2), .a(n7segalpha_2_f), .b(n7segalpha_2_e), .e(n7segalpha_2_b_2),
    .d(n7segalpha_2_c), .c(n7segalpha_2_d), .dp(in_18));
  _7_Segment_Display u_7_segment_display_3 (
    .g(n7segment_1_g), .f(n7segment_1_f), .a(n7segment_1_a_2), .b(n7segment_1_b_2), .e(n7segment_1_e),
    .d(n7segment_1_d_2), .c(n7segment_1_c_2), .dp(in_22));
  _7_Segment_Display u_7_segment_display_4 (
    .g(n7segment_2_g), .f(n7segment_2_f), .a(n7segment_2_a_2), .b(n7segment_2_b_2), .e(n7segment_2_e),
    .d(n7segment_2_d_2), .c(n7segment_2_c_2), .dp(in_27));
  _7_Segment_Display u_7_segment_display_5 (
    .g(n7segment_3_g), .f(n7segment_3_f), .a(n7segment_3_a_2), .b(n7segment_3_b_2), .e(n7segment_3_e),
    .d(n7segment_3_d_2), .c(n7segment_3_c_2), .dp(in_32));
  _7_Segment_Display u_7_segment_display_6 (
    .g(n7segment_4_g), .f(n7segment_4_f), .a(n7segment_4_a_2), .b(n7segment_4_b_2), .e(n7segment_4_e),
    .d(n7segment_4_d_2), .c(n7segment_4_c_2), .dp(in_8));
  _7segAlpha u_7segalpha_2 (
    .A(in_19), .B(in_17), .a_2(n7segalpha_2_a_2), .b_2(n7segalpha_2_b_2), .c(n7segalpha_2_c),
    .d(n7segalpha_2_d), .e(n7segalpha_2_e), .f(n7segalpha_2_f), .g(n7segalpha_2_g));
  _7segment u_7segment_1 (
    .D(in_24), .C(in_23), .B(in_21), .A(in_20), .a_2(n7segment_1_a_2), .b_2(n7segment_1_b_2),
    .c_2(n7segment_1_c_2), .d_2(n7segment_1_d_2), .e(n7segment_1_e), .f(n7segment_1_f), .g(n7segment_1_g));
  _7segment u_7segment_2 (
    .D(in_29), .C(in_28), .B(in_26), .A(in_25), .a_2(n7segment_2_a_2), .b_2(n7segment_2_b_2),
    .c_2(n7segment_2_c_2), .d_2(n7segment_2_d_2), .e(n7segment_2_e), .f(n7segment_2_f), .g(n7segment_2_g));
  _7segment u_7segment_3 (
    .D(in_34), .C(in_33), .B(in_31), .A(in_30), .a_2(n7segment_3_a_2), .b_2(n7segment_3_b_2),
    .c_2(n7segment_3_c_2), .d_2(n7segment_3_d_2), .e(n7segment_3_e), .f(n7segment_3_f), .g(n7segment_3_g));
  _7segment u_7segment_4 (
    .D(in_15), .C(in_12), .B(in_4), .A(in_1), .a_2(n7segment_4_a_2), .b_2(n7segment_4_b_2),
    .c_2(n7segment_4_c_2), .d_2(n7segment_4_d_2), .e(n7segment_4_e), .f(n7segment_4_f), .g(n7segment_4_g));
  _7_Segment_Display u_7_segment_display_7 (
    .g(n7segment_5_g), .f(n7segment_5_f), .a(n7segment_5_a_2), .b(n7segment_5_b_2), .e(n7segment_5_e),
    .d(n7segment_5_d_2), .c(n7segment_5_c_2), .dp(in_9));
  _7segment u_7segment_5 (
    .D(in_16), .C(in_13), .B(in_5), .A(in_2), .a_2(n7segment_5_a_2), .b_2(n7segment_5_b_2),
    .c_2(n7segment_5_c_2), .d_2(n7segment_5_d_2), .e(n7segment_5_e), .f(n7segment_5_f), .g(n7segment_5_g));
  _7_Segment_Display u_7_segment_display_8 (
    .g(n7segalpha_3_g), .f(n7segalpha_3_a_2), .a(n7segalpha_3_f), .b(n7segalpha_3_e), .e(n7segalpha_3_b_2),
    .d(n7segalpha_3_c), .c(n7segalpha_3_d), .dp(in_10));
  _7segAlpha u_7segalpha_3 (
    .A(in_14), .B(in_6), .a_2(n7segalpha_3_a_2), .b_2(n7segalpha_3_b_2), .c(n7segalpha_3_c),
    .d(n7segalpha_3_d), .e(n7segalpha_3_e), .f(n7segalpha_3_f), .g(n7segalpha_3_g));

  // Notes on the sheet:
  //   U
  //   a
  //   b
  //   c
  //   d
  //   e
  //   f
  //   g
  //   S
  //   0
  //   9
  //   3
  //   2
  //   a
  //   b
  //   c
  //   d
  //   e
  //   f
  //   g
  //   a
  //   b
  //   c
  //   d
  //   e
  //   f
  //   g
  //   a
  //   b
  //   c
  //   d
  //   e
  //   f
  //   g
  //   a
  //   b
  //   c
  //   d
  //   e
  //   f
  //   g
  //   a
  //   b
  //   c
  //   d
  //   e
  //   f
  //   g
  //   0
  //   a
  //   b
  //   c
  //   d
  //   e
  //   f
  //   g
  //   C
  //   a
  //   b
  //   c
  //   d
  //   e
  //   f
  //   g
endmodule

module _7segment (
  input  D,
  input  C,
  input  B,
  input  A,
  output a_2,
  output b_2,
  output c_2,
  output d_2,
  output e,
  output f,
  output g
);

  wire and_1_out, and_2_out, and_3_out, and_4_out, and_5_out, and_6_out, and_7_out, and_8_out, and_9_out,
       and_10_out, and_11_out, and_12_out, and_13_out, and_14_out, and_15_out, and_16_out, and_17_out,
       not_1_out, not_2_out, not_3_out, not_4_out, not_5_out, not_6_out, not_7_out, not_8_out, not_9_out,
       not_10_out, not_11_out, not_12_out, not_13_out, not_14_out, not_15_out, not_16_out, not_17_out,
       not_18_out, not_19_out, not_20_out, not_21_out, or_1_out, or_2_out, or_3_out, or_4_out, or_6_out,
       or_8_out, or_9_out, or_10_out, or_11_out, or_14_out, or_15_out;

  not not_1 (not_1_out, C);
  and and_1 (and_1_out, not_1_out, not_2_out);
  not not_2 (not_2_out, A);
  and and_2 (and_2_out, C, A);
  not not_3 (not_3_out, C);
  not not_4 (not_4_out, B);
  and and_3 (and_3_out, not_4_out, not_5_out);
  not not_5 (not_5_out, A);
  not not_6 (not_6_out, B);
  or or_1 (or_1_out, not_6_out, A);
  not not_7 (not_7_out, C);
  and and_4 (and_4_out, not_7_out, not_8_out);
  not not_8 (not_8_out, A);
  not not_9 (not_9_out, C);
  and and_5 (and_5_out, not_9_out, B);
  not not_10 (not_10_out, A);
  and and_6 (and_6_out, C, not_11_out);
  not not_11 (not_11_out, B);
  not not_12 (not_12_out, C);
  and and_7 (and_7_out, not_12_out, not_13_out);
  not not_13 (not_13_out, A);
  and and_8 (and_8_out, B, not_14_out);
  not not_14 (not_14_out, A);
  not not_15 (not_15_out, B);
  and and_9 (and_9_out, not_15_out, not_16_out);
  not not_16 (not_16_out, A);
  and and_10 (and_10_out, C, not_17_out);
  not not_17 (not_17_out, B);
  and and_11 (and_11_out, C, not_18_out);
  not not_18 (not_18_out, A);
  not not_19 (not_19_out, C);
  and and_12 (and_12_out, not_19_out, B);
  and and_13 (and_13_out, C, not_20_out);
  not not_20 (not_20_out, B);
  and and_14 (and_14_out, C, not_21_out);
  not not_21 (not_21_out, A);
  or or_2 (or_2_out, and_1_out, B);
  or or_3 (or_3_out, and_2_out, D);
  or or_4 (or_4_out, not_3_out, and_3_out);
  and and_15 (and_15_out, B, A);
  or or_5 (c_2, or_1_out, C);
  or or_6 (or_6_out, and_4_out, and_5_out);
  and and_16 (and_16_out, B, not_10_out);
  and and_17 (and_17_out, and_6_out, A);
  or or_7 (e, and_7_out, and_8_out);
  or or_8 (or_8_out, and_9_out, and_10_out);
  or or_9 (or_9_out, and_11_out, D);
  or or_10 (or_10_out, and_12_out, and_13_out);
  or or_11 (or_11_out, and_14_out, D);
  or or_12 (a_2, or_2_out, or_3_out);
  or or_13 (b_2, or_4_out, and_15_out);
  or or_14 (or_14_out, or_6_out, and_16_out);
  or or_15 (or_15_out, and_17_out, D);
  or or_16 (f, or_8_out, or_9_out);
  or or_17 (g, or_10_out, or_11_out);
  or or_18 (d_2, or_14_out, or_15_out);
endmodule

module _7segAlpha (
  input  A,
  input  B,
  output a_2,
  output b_2,
  output c,
  output d,
  output e,
  output f,
  output g
);

  wire not_3_out, not_4_out;

  not not_1 (b_2, A);
  not not_2 (d, B);
  not not_3 (not_3_out, A);
  not not_4 (not_4_out, B);
  or or_1 (f, B, A);
  and and_1 (e, not_3_out, not_4_out);

  assign a_2 = 1'b1;
  assign c = 1'b1;
  assign g = A;
endmodule
