// Logisim project 16 bit alu.circ as structural Verilog: 3 circuits, main circuit main
module adder (
  input  B,
  input  A,
  input  Carry_In,
  input  [1:0] Operator,
  input  Binvert,
  output Result,
  output Carry_Out
);

  wire adder_1_out, and_1_out, multiplexer_1_out, not_1_out, or_1_out;

  not not_1 (not_1_out, B);
  Multiplexer multiplexer_1 (.in0(not_1_out), .in1(B), .out(multiplexer_1_out), .sel(Binvert));  // open: en
  and and_1 (and_1_out, A, multiplexer_1_out);
  or or_1 (or_1_out, A, multiplexer_1_out);
  Adder #(.width(1)) adder_1 (.a(A), .b(multiplexer_1_out), .out(adder_1_out), .cin(Carry_In), .cout(Carry_Out));
  Multiplexer #(.select(2)) multiplexer_2 (
    .in0(and_1_out), .in1(or_1_out), .in2(adder_1_out), .out(Result), .sel(Operator));  // open: in3, en
endmodule

// 16-bit ALU
module main (
  input  in_1,
  input  [15:0] in_2,
  input  in_3,
  input  [15:0] in_4,
  input  [1:0] in_5,
  output [15:0] out_6,
  output out_7,
  output out_8,
  output out_9
);

  wire adder_1_carry_out, adder_2_carry_out, adder_3_carry_out, adder_4_carry_out, adder_5_carry_out,
       adder_6_carry_out, adder_7_carry_out, adder_8_carry_out, adder_9_carry_out, adder_10_carry_out,
       adder_11_carry_out, adder_12_carry_out, adder_13_carry_out, adder_14_carry_out, adder_15_carry_out;

  adder adder_1 (
    .Carry_In(in_1), .B(in_4[0]), .A(in_2[0]), .Binvert(in_3), .Carry_Out(adder_1_carry_out),
    .Operator(in_5), .Result(out_6[0]));
  adder adder_2 (
    .Carry_In(adder_1_carry_out), .B(in_4[1]), .A(in_2[1]), .Binvert(in_3), .Carry_Out(adder_2_carry_out),
    .Operator(in_5), .Result(out_6[1]));
  adder adder_3 (
    .Carry_In(adder_2_carry_out), .B(in_4[2]), .A(in_2[2]), .Binvert(in_3), .Carry_Out(adder_3_carry_out),
    .Operator(in_5), .Result(out_6[2]));
  adder adder_4 (
    .Carry_In(adder_3_carry_out), .B(in_4[3]), .A(in_2[3]), .Binvert(in_3), .Carry_Out(adder_4_carry_out),
    .Operator(in_5), .Result(out_6[3]));
  adder adder_5 (
    .Carry_In(adder_4_carry_out), .B(in_4[4]), .A(in_2[4]), .Binvert(in_3), .Carry_Out(adder_5_carry_out),
    .Operator(in_5), .Result(out_6[4]));
  adder adder_6 (
    .Carry_In(adder_5_carry_out), .B(in_4[5]), .A(in_2[5]), .Binvert(in_3), .Carry_Out(adder_6_carry_out),
    .Operator(in_5), .Result(out_6[5]));
  adder adder_7 (
    .Carry_In(adder_6_carry_out), .B(in_4[6]), .A(in_2[6]), .Binvert(in_3), .Carry_Out(adder_7_carry_out),
    .Operator(in_5), .Result(out_6[6]));
  adder adder_8 (
    .Carry_In(adder_7_carry_out), .B(in_4[7]), .A(in_2[7]), .Binvert(in_3), .Carry_Out(adder_8_carry_out),
    .Operator(in_5), .Result(out_6[7]));
  adder adder_9 (
    .Carry_In(adder_8_carry_out), .B(in_4[8]), .A(in_2[8]), .Binvert(in_3), .Carry_Out(adder_9_carry_out),
    .Operator(in_5), .Result(out_6[8]));
  adder adder_10 (
    .Carry_In(adder_9_carry_out), .B(in_4[9]), .A(in_2[9]), .Binvert(in_3), .Carry_Out(adder_10_carry_out),
    .Operator(in_5), .Result(out_6[9]));
  adder adder_11 (
    .Carry_In(adder_10_carry_out), .B(in_4[10]), .A(in_2[10]), .Binvert(in_3),
    .Carry_Out(adder_11_carry_out), .Operator(in_5), .Result(out_6[10]));
  adder adder_12 (
    .Carry_In(adder_11_carry_out), .B(in_4[11]), .A(in_2[11]), .Binvert(in_3),
    .Carry_Out(adder_12_carry_out), .Operator(in_5), .Result(out_6[11]));
  adder adder_13 (
    .Carry_In(adder_12_carry_out), .B(in_4[12]), .A(in_2[12]), .Binvert(in_3),
    .Carry_Out(adder_13_carry_out), .Operator(in_5), .Result(out_6[12]));
  adder adder_14 (
    .Carry_In(adder_13_carry_out), .B(in_4[13]), .A(in_2[13]), .Binvert(in_3),
    .Carry_Out(adder_14_carry_out), .Operator(in_5), .Result(out_6[13]));
  adder adder_15 (
    .Carry_In(adder_14_carry_out), .B(in_4[14]), .A(in_2[14]), .Binvert(in_3),
    .Carry_Out(adder_15_carry_out), .Operator(in_5), .Result(out_6[14]));
  adder adder_16 (
    .Carry_In(adder_15_carry_out), .B(in_4[15]), .A(in_2[15]), .Binvert(in_3), .Carry_Out(out_9),
    .Operator(in_5), .Result(out_6[15]));
  xor xor_1 (out_8, adder_15_carry_out, out_9);
  nor nor_1 (out_7, out_6[0], out_6[1], out_6[2], out_6[3], out_6[4], out_6[5], out_6[6], out_6[7], out_6[8], out_6[9], out_6[10], out_6[11], out_6[12], out_6[13], out_6[14], out_6[15]);

  // Other names for the same wires on the sheet: A0 = in_2[0]; A1 = in_2[1]; A2 = in_2[2]; A3 = in_2[3]; A4 = in_2[4];
  //   A5 = in_2[5]; A6 = in_2[6]; A7 = in_2[7]; A8 = in_2[8]; A9 = in_2[9]; A10 = in_2[10]; A11 = in_2[11];
  //   A12 = in_2[12]; A13 = in_2[13]; A14 = in_2[14]; A15 = in_2[15]; B0 = in_4[0]; B1 = in_4[1]; B2 = in_4[2];
  //   B3 = in_4[3]; B4 = in_4[4]; B5 = in_4[5]; B6 = in_4[6]; B7 = in_4[7]; B8 = in_4[8]; B9 = in_4[9];
  //   B10 = in_4[10]; B11 = in_4[11]; B12 = in_4[12]; B13 = in_4[13]; B14 = in_4[14]; B15 = in_4[15]
endmodule

module _16_Bit_ALU (
  input  Carry_In,
  input  [15:0] in_2,
  input  [15:0] in_3,
  input  Binvert,
  input  [1:0] Operator,
  output [15:0] Result,
  output Zero,
  output out_8,
  output Carry_Out
);

  main main_1 (
    .in_1(Carry_In), .in_2(in_2), .in_3(Binvert), .in_4(in_3), .in_5(Operator), .out_6(Result), .out_7(Zero),
    .out_8(out_8), .out_9(Carry_Out));
endmodule
