// Logisim project U20CS110_Assign8_CO.circ as structural Verilog: 1 circuit, main circuit main
module main (
  input  Cin,
  input  S2,
  input  [15:0] A_INPUT,
  input  S1,
  input  S0,
  input  in_6,
  input  [7:0] in_7,
  input  [15:0] B_INPUT,
  input  in_9,
  input  in_10,
  input  [7:0] in_11,
  input  in_12,
  input  [15:0] FOR_ADDI_VALUE,
  output out_14
);

  wire adder_1_cout, adder_1_out, adder_2_cout, adder_2_out, adder_3_cout, adder_3_out, adder_4_cout,
       adder_4_out, adder_5_cout, adder_5_out, adder_6_cout, adder_6_out, adder_7_cout, adder_7_out,
       adder_8_cout, adder_8_out, adder_9_cout, adder_9_out, adder_10_cout, adder_10_out, adder_11_cout,
       adder_11_out, adder_12_cout, adder_12_out, adder_13_cout, adder_13_out, adder_14_cout, adder_14_out,
       adder_15_cout, adder_15_out, adder_16_cout, adder_16_out, and_1_out, and_2_out, and_3_out, and_4_out,
       and_5_out, and_6_out, and_7_out, and_8_out, and_9_out, and_10_out, and_11_out, and_12_out, and_13_out,
       and_14_out, and_15_out, and_16_out, and_17_out, and_18_out, and_19_out, and_20_out, and_21_out,
       and_22_out, and_23_out, and_24_out, and_25_out, and_26_out, and_27_out, and_28_out, and_29_out,
       and_30_out, and_31_out, and_32_out, and_33_out, and_34_out, and_35_out, and_36_out, and_37_out,
       and_38_out, and_39_out, and_40_out, and_41_out, and_42_out, and_43_out, and_44_out, and_45_out,
       and_46_out, and_47_out, and_48_out, and_49_out, and_50_out, and_51_out, and_52_out, and_53_out,
       and_54_out, and_55_out, and_56_out, and_57_out, and_58_out, and_59_out, and_60_out, and_61_out,
       and_62_out, and_63_out, and_64_out, and_65_out, and_66_out, and_67_out, and_68_out, and_69_out,
       and_70_out, and_71_out, and_72_out, and_73_out, and_74_out, and_75_out, and_76_out, and_77_out,
       and_78_out, and_79_out, and_80_out, and_81_out, and_82_out, button_1_out, button_2_out, button_3_out,
       not_1_out, not_2_out, not_3_out, not_4_out, not_5_out, not_6_out, not_7_out, not_8_out, not_9_out,
       not_10_out, not_11_out, not_12_out, not_13_out, not_14_out, not_15_out, not_16_out, not_17_out,
       not_18_out, not_19_out, not_20_out, not_21_out, or_1_out, or_2_out, or_3_out, or_4_out, or_5_out,
       or_6_out, or_7_out, or_8_out, or_9_out, or_10_out, or_11_out, or_12_out, or_13_out, or_14_out,
       or_15_out, or_16_out, or_17_out, or_18_out, or_19_out, or_20_out, or_21_out, or_22_out, or_23_out,
       or_24_out, or_25_out, or_26_out, or_27_out, or_28_out, or_29_out, or_30_out, or_31_out, or_32_out,
       or_33_out, or_34_out, or_35_out, or_36_out, or_37_out, or_38_out, or_39_out, or_40_out, or_41_out,
       or_42_out, or_43_out, or_44_out, or_45_out, or_46_out, or_47_out, or_48_out;
  wire [15:0] controlled_buffer_1_out, controlled_buffer_2_out;

  assign controlled_buffer_1_out = in_10 ? B_INPUT : 16'bz;  // Controlled_Buffer controlled_buffer_1
  not not_1 (not_1_out, in_10);
  Button button_1 (.out(button_1_out));
  RAM #(.dataWidth(16)) ram_1 (
    .addr(in_11), .data(controlled_buffer_1_out), .sel(1'b1), .clk(button_1_out), .ld(not_1_out), .clr(in_12));
  assign controlled_buffer_2_out = in_6 ? A_INPUT : 16'bz;  // Controlled_Buffer controlled_buffer_2
  not not_2 (not_2_out, in_6);
  RAM #(.dataWidth(16)) ram_2 (
    .addr(in_7), .data(controlled_buffer_2_out), .sel(1'b1), .clk(button_2_out), .ld(not_2_out), .clr(in_9));
  Button button_2 (.out(button_2_out));
  not not_3 (not_3_out, S2);
  or or_1 (or_1_out, controlled_buffer_1_out[0], FOR_ADDI_VALUE[0]);
  or or_2 (or_2_out, controlled_buffer_1_out[1], FOR_ADDI_VALUE[1]);
  not not_4 (not_4_out, or_2_out);
  or or_3 (or_3_out, controlled_buffer_1_out[2], FOR_ADDI_VALUE[2]);
  not not_5 (not_5_out, or_3_out);
  or or_4 (or_4_out, controlled_buffer_1_out[3], FOR_ADDI_VALUE[3]);
  or or_5 (or_5_out, controlled_buffer_1_out[4], FOR_ADDI_VALUE[4]);
  or or_6 (or_6_out, controlled_buffer_1_out[5], FOR_ADDI_VALUE[5]);
  or or_7 (or_7_out, controlled_buffer_1_out[6], FOR_ADDI_VALUE[6]);
  or or_8 (or_8_out, controlled_buffer_1_out[7], FOR_ADDI_VALUE[7]);
  or or_9 (or_9_out, controlled_buffer_1_out[8], FOR_ADDI_VALUE[8]);
  or or_10 (or_10_out, controlled_buffer_1_out[9], FOR_ADDI_VALUE[9]);
  or or_11 (or_11_out, controlled_buffer_1_out[10], FOR_ADDI_VALUE[10]);
  or or_12 (or_12_out, controlled_buffer_1_out[11], FOR_ADDI_VALUE[11]);
  or or_13 (or_13_out, controlled_buffer_1_out[12], FOR_ADDI_VALUE[12]);
  or or_14 (or_14_out, controlled_buffer_1_out[13], FOR_ADDI_VALUE[13]);
  or or_15 (or_15_out, controlled_buffer_1_out[14], FOR_ADDI_VALUE[14]);
  or or_16 (or_16_out, controlled_buffer_1_out[15], FOR_ADDI_VALUE[15]);
  not not_6 (not_6_out, or_1_out);
  not not_7 (not_7_out, or_4_out);
  not not_8 (not_8_out, or_5_out);
  not not_9 (not_9_out, or_6_out);
  not not_10 (not_10_out, or_7_out);
  not not_11 (not_11_out, or_8_out);
  not not_12 (not_12_out, or_9_out);
  not not_13 (not_13_out, or_10_out);
  not not_14 (not_14_out, or_11_out);
  not not_15 (not_15_out, or_12_out);
  not not_16 (not_16_out, or_13_out);
  not not_17 (not_17_out, or_14_out);
  not not_18 (not_18_out, or_15_out);
  not not_19 (not_19_out, or_16_out);
  not not_20 (not_20_out, S0);
  and and_1 (and_1_out, not_20_out, S1, S2);
  not not_21 (not_21_out, S1);
  and and_2 (and_2_out, not_20_out, not_21_out, S2);
  and and_3 (and_3_out, and_2_out, or_1_out);
  and and_4 (and_4_out, and_1_out, not_6_out);
  and and_5 (and_5_out, or_1_out, S0);
  and and_6 (and_6_out, not_6_out, S1);
  and and_7 (and_7_out, and_2_out, or_2_out);
  and and_8 (and_8_out, and_1_out, not_4_out);
  and and_9 (and_9_out, or_2_out, S0);
  and and_10 (and_10_out, not_4_out, S1);
  and and_11 (and_11_out, and_2_out, or_3_out);
  and and_12 (and_12_out, and_1_out, not_5_out);
  and and_13 (and_13_out, or_3_out, S0);
  and and_14 (and_14_out, not_5_out, S1);
  and and_15 (and_15_out, and_2_out, or_4_out);
  and and_16 (and_16_out, and_1_out, not_7_out);
  and and_17 (and_17_out, or_4_out, S0);
  and and_18 (and_18_out, not_7_out, S1);
  and and_19 (and_19_out, and_2_out, or_5_out);
  and and_20 (and_20_out, and_1_out, not_8_out);
  and and_21 (and_21_out, or_5_out, S0);
  and and_22 (and_22_out, not_8_out, S1);
  and and_23 (and_23_out, and_2_out, or_6_out);
  and and_24 (and_24_out, and_1_out, not_9_out);
  and and_25 (and_25_out, or_6_out, S0);
  and and_26 (and_26_out, not_9_out, S1);
  and and_27 (and_27_out, and_2_out, or_7_out);
  and and_28 (and_28_out, and_1_out, not_10_out);
  and and_29 (and_29_out, or_7_out, S0);
  and and_30 (and_30_out, not_10_out, S1);
  and and_31 (and_31_out, and_2_out, or_8_out);
  and and_32 (and_32_out, and_1_out, not_11_out);
  and and_33 (and_33_out, or_8_out, S0);
  and and_34 (and_34_out, not_11_out, S1);
  and and_35 (and_35_out, and_2_out, or_9_out);
  and and_36 (and_36_out, and_1_out, not_12_out);
  and and_37 (and_37_out, or_9_out, S0);
  and and_38 (and_38_out, not_12_out, S1);
  and and_39 (and_39_out, and_2_out, or_10_out);
  and and_40 (and_40_out, and_1_out, not_13_out);
  and and_41 (and_41_out, or_10_out, S0);
  and and_42 (and_42_out, not_13_out, S1);
  and and_43 (and_43_out, and_2_out, or_11_out);
  and and_44 (and_44_out, and_1_out, not_14_out);
  and and_45 (and_45_out, or_11_out, S0);
  and and_46 (and_46_out, not_14_out, S1);
  and and_47 (and_47_out, and_2_out, or_12_out);
  and and_48 (and_48_out, and_1_out, not_15_out);
  and and_49 (and_49_out, or_12_out, S0);
  and and_50 (and_50_out, not_15_out, S1);
  and and_51 (and_51_out, and_2_out, or_13_out);
  and and_52 (and_52_out, and_1_out, not_16_out);
  and and_53 (and_53_out, or_13_out, S0);
  and and_54 (and_54_out, not_16_out, S1);
  and and_55 (and_55_out, and_2_out, or_14_out);
  and and_56 (and_56_out, and_1_out, not_17_out);
  and and_57 (and_57_out, or_14_out, S0);
  and and_58 (and_58_out, not_17_out, S1);
  and and_59 (and_59_out, and_2_out, or_15_out);
  and and_60 (and_60_out, and_1_out, not_18_out);
  and and_61 (and_61_out, or_15_out, S0);
  and and_62 (and_62_out, not_18_out, S1);
  and and_63 (and_63_out, or_15_out, or_16_out);
  and and_64 (and_64_out, and_1_out, not_19_out);
  and and_65 (and_65_out, or_16_out, S0);
  and and_66 (and_66_out, not_19_out, S1);
  or or_17 (or_17_out, and_3_out, and_4_out, controlled_buffer_2_out[0]);
  or or_18 (or_18_out, and_5_out, and_6_out);
  or or_19 (or_19_out, and_7_out, and_8_out, controlled_buffer_2_out[1]);
  or or_20 (or_20_out, and_9_out, and_10_out);
  or or_21 (or_21_out, and_11_out, and_12_out, controlled_buffer_2_out[2]);
  or or_22 (or_22_out, and_13_out, and_14_out);
  or or_23 (or_23_out, and_15_out, and_16_out, controlled_buffer_2_out[3]);
  or or_24 (or_24_out, and_17_out, and_18_out);
  or or_25 (or_25_out, and_19_out, and_20_out, controlled_buffer_2_out[4]);
  or or_26 (or_26_out, and_21_out, and_22_out);
  or or_27 (or_27_out, and_27_out, and_28_out, controlled_buffer_2_out[6]);
  or or_28 (or_28_out, and_29_out, and_30_out);
  or or_29 (or_29_out, and_31_out, and_32_out, controlled_buffer_2_out[7]);
  or or_30 (or_30_out, and_33_out, and_34_out);
  or or_31 (or_31_out, and_39_out, and_40_out, controlled_buffer_2_out[9]);
  or or_32 (or_32_out, and_41_out, and_42_out);
  or or_33 (or_33_out, and_43_out, and_44_out, controlled_buffer_2_out[10]);
  or or_34 (or_34_out, and_45_out, and_46_out);
  or or_35 (or_35_out, and_51_out, and_52_out, controlled_buffer_2_out[12]);
  or or_36 (or_36_out, and_53_out, and_54_out);
  or or_37 (or_37_out, and_55_out, and_56_out, controlled_buffer_2_out[13]);
  or or_38 (or_38_out, and_57_out, and_58_out);
  or or_39 (or_39_out, and_63_out, and_64_out, controlled_buffer_2_out[15]);
  or or_40 (or_40_out, and_65_out, and_66_out);
  or or_41 (or_41_out, and_23_out, and_24_out, controlled_buffer_2_out[5]);
  or or_42 (or_42_out, and_25_out, and_26_out);
  or or_43 (or_43_out, and_35_out, and_36_out, controlled_buffer_2_out[8]);
  or or_44 (or_44_out, and_37_out, and_38_out);
  or or_45 (or_45_out, and_47_out, and_48_out, controlled_buffer_2_out[11]);
  or or_46 (or_46_out, and_49_out, and_50_out);
  or or_47 (or_47_out, and_59_out, and_60_out, controlled_buffer_2_out[14]);
  or or_48 (or_48_out, and_61_out, and_62_out);
  and and_67 (and_67_out, not_3_out, Cin);
  Adder #(.width(1)) adder_1 (.a(or_17_out), .b(or_18_out), .out(adder_1_out), .cin(and_67_out), .cout(adder_1_cout));
  and and_68 (and_68_out, not_3_out, adder_1_cout);
  Adder #(.width(1)) adder_2 (.a(or_19_out), .b(or_20_out), .out(adder_2_out), .cin(and_68_out), .cout(adder_2_cout));
  and and_69 (and_69_out, not_3_out, adder_2_cout);
  Adder #(.width(1)) adder_3 (.a(or_21_out), .b(or_22_out), .out(adder_3_out), .cin(and_69_out), .cout(adder_3_cout));
  and and_70 (and_70_out, not_3_out, adder_3_cout);
  Adder #(.width(1)) adder_4 (.a(or_23_out), .b(or_24_out), .out(adder_4_out), .cin(and_70_out), .cout(adder_4_cout));
  and and_71 (and_71_out, not_3_out, adder_4_cout);
  Adder #(.width(1)) adder_5 (.a(or_25_out), .b(or_26_out), .out(adder_5_out), .cin(and_71_out), .cout(adder_5_cout));
  and and_72 (and_72_out, not_3_out, adder_5_cout);
  Adder #(.width(1)) adder_6 (.a(or_41_out), .b(or_42_out), .out(adder_6_out), .cin(and_72_out), .cout(adder_6_cout));
  and and_73 (and_73_out, not_3_out, adder_6_cout);
  Adder #(.width(1)) adder_7 (.a(or_27_out), .b(or_28_out), .out(adder_7_out), .cin(and_73_out), .cout(adder_7_cout));
  and and_74 (and_74_out, not_3_out, adder_7_cout);
  Adder #(.width(1)) adder_8 (.a(or_29_out), .b(or_30_out), .out(adder_8_out), .cin(and_74_out), .cout(adder_8_cout));
  and and_75 (and_75_out, not_3_out, adder_8_cout);
  Adder #(.width(1)) adder_9 (.a(or_43_out), .b(or_44_out), .out(adder_9_out), .cin(and_75_out), .cout(adder_9_cout));
  and and_76 (and_76_out, not_3_out, adder_9_cout);
  Adder #(.width(1)) adder_10 (
    .a(or_31_out), .b(or_32_out), .out(adder_10_out), .cin(and_76_out), .cout(adder_10_cout));
  and and_77 (and_77_out, not_3_out, adder_10_cout);
  Adder #(.width(1)) adder_11 (
    .a(or_33_out), .b(or_34_out), .out(adder_11_out), .cin(and_77_out), .cout(adder_11_cout));
  and and_78 (and_78_out, not_3_out, adder_11_cout);
  Adder #(.width(1)) adder_12 (
    .a(or_45_out), .b(or_46_out), .out(adder_12_out), .cin(and_78_out), .cout(adder_12_cout));
  and and_79 (and_79_out, not_3_out, adder_12_cout);
  Adder #(.width(1)) adder_13 (
    .a(or_35_out), .b(or_36_out), .out(adder_13_out), .cin(and_79_out), .cout(adder_13_cout));
  and and_80 (and_80_out, not_3_out, adder_13_cout);
  Adder #(.width(1)) adder_14 (
    .a(or_37_out), .b(or_38_out), .out(adder_14_out), .cin(and_80_out), .cout(adder_14_cout));
  and and_81 (and_81_out, not_3_out, adder_14_cout);
  Adder #(.width(1)) adder_15 (
    .a(or_47_out), .b(or_48_out), .out(adder_15_out), .cin(and_81_out), .cout(adder_15_cout));
  and and_82 (and_82_out, not_3_out, adder_15_cout);
  Adder #(.width(1)) adder_16 (
    .a(or_39_out), .b(or_40_out), .out(adder_16_out), .cin(and_82_out), .cout(adder_16_cout));
  and and_83 (out_14, not_3_out, adder_16_cout);
  Shift_Register #(.length(16)) OUTPUT_REGISTER (
    .clk(button_3_out), .load(1'b1), .d0(adder_16_out), .d1(adder_15_out), .d2(adder_14_out),
    .d3(adder_13_out), .d4(adder_12_out), .d5(adder_11_out), .d6(adder_10_out), .d7(adder_9_out),
    .d8(adder_8_out), .d9(adder_7_out), .d10(adder_6_out), .d11(adder_5_out), .d12(adder_4_out),
    .d13(adder_3_out), .d14(adder_2_out), .d15(adder_1_out));  // open: shift, in, out, clr, q0, q1, q2, q3, q4, q5, q6, q7, q8, q9, q10, q11, q12, q13, q14, q15
  Button button_3 (.out(button_3_out));

  // Notes on the sheet:
  //   B110_Assignment 8
  //   OUTPUT IN BINARY
  //   Input-operation-table
  //   S2  S1  S0  Cin  Op
  //   0    0    1     0    ADD
  //   1    0    0     X    OR
  //   0    0    1     1    ADDI
  //   0    1    0     1    SUB
  //   1    1    1     X    NOT
  //   S2  S1  S0  Cin
endmodule
